// Logisim project Circuitos.circ as structural Verilog: 1 circuit, main circuit main
module main (
  input  p,
  input  p_2,
  input  q,
  input  in_4,
  input  r,
  input  r_2,
  input  p_3,
  input  p_4,
  input  q_2,
  input  q_3,
  input  r_3,
  input  r_4,
  output out_13,
  output out_14,
  output out_15,
  output out_16
);

  wire and_1_out, and_2_out, and_3_out, and_5_out, and_6_out, and_7_out, and_8_out, not_1_out, not_2_out,
       not_3_out, not_4_out, not_5_out, not_6_out, not_7_out, not_8_out, not_9_out, not_10_out, or_1_out,
       or_3_out;

  not not_1 (not_1_out, p);
  not not_2 (not_2_out, q);
  not not_3 (not_3_out, r);
  not not_4 (not_4_out, q_3);
  not not_5 (not_5_out, r_4);
  and and_1 (and_1_out, p_4, not_4_out);
  or or_1 (or_1_out, not_1_out, q, r);
  and and_2 (and_2_out, not_3_out, p);
  and and_3 (and_3_out, p, not_2_out);
  or or_2 (out_15, not_5_out, and_1_out);
  or or_3 (or_3_out, and_2_out, and_3_out);
  and and_4 (out_13, or_1_out, or_3_out);
  not not_6 (not_6_out, p_2);
  not not_7 (not_7_out, in_4);
  not not_8 (not_8_out, p_3);
  not not_9 (not_9_out, q_2);
  not not_10 (not_10_out, r_3);
  and and_5 (and_5_out, p_2, not_7_out);
  and and_6 (and_6_out, r_2, not_6_out);
  and and_7 (and_7_out, not_8_out, not_9_out);
  and and_8 (and_8_out, p_3, q_2);
  or or_4 (out_14, and_5_out, and_6_out);
  or or_5 (out_16, not_10_out, and_7_out, and_8_out);

  // Notes on the sheet:
  //   (p->q)->-,r
  //   (q+r+~p)*((~r*p)+(p*~q))
  //   (p~q)+(r~p)
  //   pq+~r+~q~p
endmodule
