// Logisim project P4.circ as structural Verilog: 1 circuit, main circuit main
module main (
  input  p,
  input  p_2,
  input  q,
  input  q_2,
  input  r,
  input  r_2,
  input  s,
  input  p_3,
  input  q_3,
  input  T,
  input  r_3,
  input  Q_4,
  input  s_2,
  input  R_4,
  input  P_4,
  input  S_3,
  output out_17,
  output out_18,
  output out_19,
  output out_20
);

  wire and_1_out, and_2_out, and_3_out, and_4_out, and_5_out, and_6_out, and_7_out, and_8_out, and_9_out,
       and_10_out, and_11_out, and_12_out, and_13_out, not_1_out, not_2_out, not_3_out, not_4_out, not_5_out,
       not_6_out, not_7_out, not_8_out, not_9_out, not_10_out, not_11_out, not_12_out;

  and and_1 (and_1_out, q_2, r_2);
  not not_1 (not_1_out, p_3);
  not not_2 (not_2_out, q_3);
  not not_3 (not_3_out, s_2);
  or or_1 (out_17, p_2, and_1_out);
  and and_2 (and_2_out, not_1_out, s_2);
  and and_3 (and_3_out, not_2_out, not_3_out);
  and and_4 (and_4_out, not_2_out, r_3);
  or or_2 (out_19, and_4_out, and_3_out, and_2_out);
  not not_4 (not_4_out, p);
  not not_5 (not_5_out, q);
  not not_6 (not_6_out, r);
  not not_7 (not_7_out, s);
  not not_8 (not_8_out, T);
  not not_9 (not_9_out, Q_4);
  not not_10 (not_10_out, R_4);
  not not_11 (not_11_out, P_4);
  not not_12 (not_12_out, S_3);
  and and_5 (and_5_out, not_7_out, p, q, r);
  and and_6 (and_6_out, p, not_5_out, r, s);
  and and_7 (and_7_out, not_6_out, p, q, s);
  and and_8 (and_8_out, not_4_out, q, r, s);
  and and_9 (and_9_out, T, not_9_out, not_10_out, S_3);
  or or_3 (out_18, and_8_out, and_6_out, and_7_out, and_5_out);
  and and_10 (and_10_out, T, Q_4, R_4, S_3);
  and and_11 (and_11_out, T, not_10_out, not_11_out, not_12_out);
  and and_12 (and_12_out, not_8_out, not_9_out, not_10_out, not_12_out);
  and and_13 (and_13_out, not_8_out, Q_4, not_10_out, not_11_out, S_3);
  or or_4 (out_20, and_13_out, and_12_out, and_11_out, and_10_out, and_9_out);

  // Notes on the sheet:
  //   p~qr+p~r+qr --> p + qr
  //   ~qr+~q~s+~ps
  //   ~TQ~R~PS+~T~Q~R~S+T~R~P~S+TQRS+T~Q~RS
  //   ~pqrs+p~qrs+pq~rs+pqr~s
endmodule
